// Logisim project FullAdderWithStaticCarry.circ as structural Verilog: 35 circuits, main circuit FA0
module FA0 (
  input  A,
  input  B,
  output s,
  output cout
);

  wire nor_1_out;

  and and_1 (cout, A, B);
  nor nor_1 (nor_1_out, A, B);
  nor nor_2 (s, nor_1_out, cout);
  PartialProduct partialproduct_1 ();  // open: a8, a7, a6, a5, a4, a3, a2, a1, b8, b7, b6, b5, b4, b3, b2, b1

  // Notes on the sheet:
  //   2.75
  //   1.75
endmodule

module FA1 (
  input  A,
  input  B,
  output s,
  output cout
);

  wire nand_1_out;

  or or_1 (cout, A, B);
  nand nand_1 (nand_1_out, B, A);
  nand nand_2 (s, cout, nand_1_out);

  // Notes on the sheet:
  //   2.75
  //   1.75
endmodule

module FAopt1 (
  input  a,
  input  b,
  input  cin,
  output s,
  output cout
);

  wire nand_1_out, nand_2_out, nor_1_out, nor_2_out, nor_3_out, not_1_out, not_2_out;

  nor nor_1 (nor_1_out, a, b);
  not not_1 (not_1_out, nand_1_out);
  nand nand_1 (nand_1_out, b, a);
  nor nor_2 (nor_2_out, nor_1_out, not_1_out);
  nor nor_3 (nor_3_out, nor_2_out, cin);
  nor nor_4 (s, nor_3_out, not_2_out);
  not not_2 (not_2_out, nand_2_out);
  nand nand_2 (nand_2_out, nor_2_out, cin);
  nand nand_3 (cout, nand_2_out, nand_1_out);

  // Notes on the sheet:
  //   0
  //   0
  //   32 Transistors
  //   FAopt1
  //   else: cin + 2.75
  //   else: cin + 2
  //   5.5 if cin < 2.75
  //   4.75 if cin < 2.75
endmodule

module FAopt2 (
  input  a,
  input  b,
  input  cin,
  output s,
  output cout
);

  wire and_1_out, nand_1_out, nand_2_out, nand_3_out, nor_1_out, nor_2_out, nor_3_out, not_1_out;

  nor nor_1 (nor_1_out, a, b);
  not not_1 (not_1_out, nand_1_out);
  nor nor_2 (nor_2_out, nor_1_out, not_1_out);
  nand nand_1 (nand_1_out, a, b);
  nand nand_2 (nand_2_out, b, cin);
  nand nand_3 (nand_3_out, a, cin);
  and and_1 (and_1_out, nor_2_out, cin);
  nor nor_3 (nor_3_out, nor_2_out, cin);
  nand nand_4 (cout, nand_1_out, nand_2_out, nand_3_out);
  nor nor_4 (s, nor_3_out, and_1_out);

  // Notes on the sheet:
  //   0
  //   0
  //   FAopt2
  //   42 transistors
  //   else: cin + 2.75
  //   5.5 if cin < 2.75
  //   2.25 + cin
endmodule

module RippleCarryAdders (
  input  [3:0] A,
  input  [3:0] B,
  output [3:0] S,
  output COUT
);

  wire fa0_1_cout, faopt1_2_cout, faopt2_1_cout;

  FAopt1 faopt1_1 (.cout(COUT), .s(S[3]), .cin(faopt1_2_cout), .a(A[3]), .b(B[3]));
  FAopt1 faopt1_2 (.cout(faopt1_2_cout), .s(S[2]), .cin(faopt2_1_cout), .a(A[2]), .b(B[2]));
  FAopt2 faopt2_1 (.s(S[1]), .cout(faopt2_1_cout), .b(B[1]), .cin(fa0_1_cout), .a(A[1]));
  FA0 fa0_1 (.s(S[0]), .cout(fa0_1_cout), .A(A[0]), .B(B[0]));

  // Notes on the sheet:
  //   8
  //   6
  //   8.75
  //   4
  //   6.75
  //   5.5
  //   1.75
  //   5.5
endmodule

module EightBitRipple (
  input  [7:0] in_1,
  input  [7:0] in_2,
  output [7:0] _16_75,
  output cout
);

  wire fa0_1_cout, faopt1_3_cout, faopt1_4_cout, faopt1_5_cout, faopt1_6_cout, faopt2_1_cout;

  FAopt1 faopt1_1 (.cout(cout), .s(_16_75[7]), .cin(in_1[7]), .a(in_1[7]), .b(in_2[7]));
  FAopt1 faopt1_2 (.cout(in_1[7]), .s(_16_75[6]), .cin(faopt1_3_cout), .a(in_1[6]), .b(in_2[6]));
  FAopt1 faopt1_3 (.cout(faopt1_3_cout), .s(_16_75[5]), .cin(faopt1_4_cout), .a(in_1[5]), .b(in_2[5]));
  FAopt1 faopt1_4 (.cout(faopt1_4_cout), .s(_16_75[4]), .cin(faopt1_5_cout), .a(in_1[4]), .b(in_2[4]));
  FAopt1 faopt1_5 (.cout(faopt1_5_cout), .s(_16_75[3]), .cin(faopt1_6_cout), .a(in_1[3]), .b(in_2[3]));
  FAopt1 faopt1_6 (.cout(faopt1_6_cout), .s(_16_75[2]), .cin(faopt2_1_cout), .a(in_1[2]), .b(in_2[2]));
  FAopt2 faopt2_1 (.s(_16_75[1]), .cout(faopt2_1_cout), .b(in_2[1]), .cin(fa0_1_cout), .a(in_1[1]));
  FA0 fa0_1 (.s(_16_75[0]), .cout(fa0_1_cout), .A(in_1[0]), .B(in_2[0]));

  // Notes on the sheet:
  //   16
  //   16.75
  //   14
  //   14.75
  //   12
  //   10
  //   12.75
  //   10.75
  //   8
  //   8.75
  //   6
  //   6.75
  //   4
  //   16
  //   5.5
  //   140 transistors
  //   1.75
  //   5.5
endmodule

module Mux1 (
  input  in0,
  input  in1,
  input  ctrl,
  output out_4
);

  wire nand_1_out, nand_2_out, not_1_out;

  not not_1 (not_1_out, ctrl);
  nand nand_1 (nand_1_out, in0, not_1_out);
  nand nand_2 (nand_2_out, in1, ctrl);
  nand nand_3 (out_4, nand_1_out, nand_2_out);

  // Notes on the sheet:
  //   14 transistors
  //   Z = max(in0 + 2, in1 + 2, ctrl + 2.75)
endmodule

module mux4 (
  input  d00,
  input  d01,
  input  d10,
  input  d11,
  input  S1,
  input  S0,
  output out_7
);

  wire mux1_1_out_4, mux1_2_out_4;

  Mux1 mux1_1 (.out_4(mux1_1_out_4), .in1(d01), .in0(d00), .ctrl(S0));
  Mux1 mux1_2 (.out_4(mux1_2_out_4), .in1(d11), .in0(d10), .ctrl(S0));
  Mux1 mux1_3 (.out_4(out_7), .in1(mux1_2_out_4), .in0(mux1_1_out_4), .ctrl(S1));

  // Notes on the sheet:
  //   42 transistors
  //   z = max(in0 + 4, in01 + 4, in10 + 4, in11 + 4, ctrl1 + 4.75, ctrl0 + 4.75, ctrl1 + 2.75)
  //   s
endmodule

module mux2_1 (
  input  in0,
  input  in1,
  input  sel,
  output out_4
);

  wire not_1_out, transmission_1_p4;

  not not_1 (not_1_out, sel);
  // Transmission_Gate transmission_1: pin names not known; wires that end beside it: in0, sel, not_1_out, transmission_1_p4
  // Transmission_Gate transmission_2: pin names not known; wires that end beside it: in1, not_1_out, sel, transmission_1_p4
  not not_2 (out_4, transmission_1_p4);

  // Notes on the sheet:
  //   Z = max(sel + 1.75, in0 + 1, in1 + 1)
  //   8 transistors
endmodule

module mux2_4 (
  input  in00,
  input  in01,
  input  in10,
  input  in11,
  input  sel1,
  input  sel0,
  output out_7
);

  wire mux2_1_1_out_4, mux2_1_2_out_4;

  mux2_1 mux2_1_1 (.out_4(mux2_1_1_out_4), .in0(in00), .in1(in01), .sel(sel0));
  mux2_1 mux2_1_2 (.out_4(mux2_1_2_out_4), .in0(in10), .in1(in11), .sel(sel0));
  mux2_1 mux2_1_3 (.out_4(out_7), .in0(mux2_1_1_out_4), .in1(mux2_1_2_out_4), .sel(sel1));

  // Notes on the sheet:
  //   Z = max(in00 + 2, in01 + 2, in10 + 2, in11 + 2, sel0 + 2.75, sel1 + 1.75)
  //   34 inverters
endmodule

module CarrySelect_8 (
  input  [7:0] in_1,
  input  [7:0] in_2,
  output [7:0] sum,
  output cOut
);

  wire fa40_1_p2, fa41_1_cout, mux2_1_5_out_4, undriven;
  wire [3:0] fa40_1_p1, fa41_1_s, mux2_1_4_out_4;

  mux2_1 mux2_1_1 (.out_4(mux2_1_4_out_4[3]), .in0(fa40_1_p1[3]), .in1(fa41_1_s[3]), .sel(undriven));
  FA41 fa41_1 (.A(in_1[7:4]), .B(in_2[7:4]), .S(fa41_1_s), .COUT(fa41_1_cout));
  mux2_1 mux2_1_2 (.out_4(mux2_1_4_out_4[2]), .in0(fa40_1_p1[2]), .in1(fa41_1_s[2]), .sel(undriven));
  mux2_1 mux2_1_3 (.out_4(mux2_1_4_out_4[1]), .in0(fa40_1_p1[1]), .in1(fa41_1_s[1]), .sel(undriven));
  assign sum[7:4] = ~mux2_1_4_out_4;  // NOT_Gate not_1, 4 bits wide
  // FA40 fa40_1: pin names not known; wires that end beside it: fa40_1_p1, fa40_1_p2
  mux2_1 mux2_1_4 (.out_4(mux2_1_4_out_4[0]), .in0(fa40_1_p1[0]), .in1(fa41_1_s[0]), .sel(undriven));
  not not_2 (cOut, mux2_1_5_out_4);
  mux2_1 mux2_1_5 (.out_4(mux2_1_5_out_4), .in0(fa40_1_p2), .in1(fa41_1_cout), .sel(undriven));
  FA40 fa40_2 (.S(sum[3:0]));  // open: A, B, COUT

  // Notes on the sheet:
  //   max(8+1.75, 8.75+1)= 9.75
  //   9.75
  //   8.75
  //   10.5
  //   8
  //   10.5
endmodule

module FA40 (
  input  [3:0] A,
  input  [3:0] B,
  output [3:0] S,
  output COUT
);

  wire fa0_1_cout, faopt1_2_cout, faopt2_1_cout;

  FAopt1 faopt1_1 (.cout(COUT), .s(S[3]), .cin(faopt1_2_cout), .a(A[3]), .b(B[3]));
  FAopt1 faopt1_2 (.cout(faopt1_2_cout), .s(S[2]), .cin(faopt2_1_cout), .a(A[2]), .b(B[2]));
  FAopt2 faopt2_1 (.s(S[1]), .cout(faopt2_1_cout), .b(B[1]), .cin(fa0_1_cout), .a(A[1]));
  FA0 fa0_1 (.s(S[0]), .cout(fa0_1_cout), .A(A[0]), .B(B[0]));

  // Notes on the sheet:
  //   8
  //   6
  //   8.75
  //   4
  //   6.75
  //   5.5
  //   1.75
  //   5.5
  //   8
  //   8.75
endmodule

module FA41 (
  input  [3:0] A,
  input  [3:0] B,
  output [3:0] S,
  output COUT
);

  wire fa1_1_cout, faopt1_2_cout, faopt2_1_cout;

  FAopt1 faopt1_1 (.cout(COUT), .s(S[3]), .cin(faopt1_2_cout), .a(A[3]), .b(B[3]));
  FAopt1 faopt1_2 (.cout(faopt1_2_cout), .s(S[2]), .cin(faopt2_1_cout), .a(A[2]), .b(B[2]));
  FAopt2 faopt2_1 (.s(S[1]), .cout(faopt2_1_cout), .b(B[1]), .cin(fa1_1_cout), .a(A[1]));
  FA1 fa1_1 (.s(S[0]), .cout(fa1_1_cout), .A(A[0]), .B(B[0]));

  // Notes on the sheet:
  //   8
  //   6
  //   8.75
  //   6.75
  //   4
  //   1.75
  //   4.5
  //   2.75
endmodule

module CarrySelect_81 (
  input  [7:0] in_1,
  input  [7:0] in_2,
  output [7:0] sum,
  output cOut
);

  wire fa40_1_p2, fa41_1_cout, fa41_2_cout, mux2_1_5_out_4;
  wire [3:0] fa40_1_p1, fa41_1_s, mux2_1_4_out_4;

  mux2_1 mux2_1_1 (.out_4(mux2_1_4_out_4[3]), .in0(fa40_1_p1[3]), .in1(fa41_1_s[3]), .sel(fa41_2_cout));
  FA41 fa41_1 (.A(in_1[7:4]), .B(in_2[7:4]), .S(fa41_1_s), .COUT(fa41_1_cout));
  mux2_1 mux2_1_2 (.out_4(mux2_1_4_out_4[2]), .in0(fa40_1_p1[2]), .in1(fa41_1_s[2]), .sel(fa41_2_cout));
  mux2_1 mux2_1_3 (.out_4(mux2_1_4_out_4[1]), .in0(fa40_1_p1[1]), .in1(fa41_1_s[1]), .sel(fa41_2_cout));
  assign sum[7:4] = ~mux2_1_4_out_4;  // NOT_Gate not_1, 4 bits wide
  // FA40 fa40_1: pin names not known; wires that end beside it: fa40_1_p1, fa40_1_p2
  mux2_1 mux2_1_4 (.out_4(mux2_1_4_out_4[0]), .in0(fa40_1_p1[0]), .in1(fa41_1_s[0]), .sel(fa41_2_cout));
  not not_2 (cOut, mux2_1_5_out_4);
  mux2_1 mux2_1_5 (.out_4(mux2_1_5_out_4), .in0(fa40_1_p2), .in1(fa41_1_cout), .sel(fa41_2_cout));
  FA41 fa41_2 (.A(in_1[3:0]), .B(in_2[3:0]), .S(sum[3:0]), .COUT(fa41_2_cout));

  // Notes on the sheet:
  //   max(8+1.75, 8.75+1)= 9.75
  //   9.75
  //   8.75
  //   10.5
  //   8
  //   10.5
endmodule

module CarrySelect_16 (
  input  [15:0] in_1,
  input  [15:0] in_2,
  output [15:0] out_3,
  output out_4
);

  wire carryselect_8_1_cout, carryselect_8_2_cout, carryselect_81_1_cout, mux2_1_6_out_4;
  wire [7:0] carryselect_8_1_sum, carryselect_81_1_sum, mux2_1_9_out_4;

  mux2_1 mux2_1_1 (
    .out_4(mux2_1_9_out_4[7]), .in0(carryselect_8_1_sum[7]), .in1(carryselect_81_1_sum[7]),
    .sel(carryselect_8_2_cout));
  mux2_1 mux2_1_2 (
    .out_4(mux2_1_9_out_4[6]), .in0(carryselect_8_1_sum[6]), .in1(carryselect_81_1_sum[6]),
    .sel(carryselect_8_2_cout));
  CarrySelect_81 carryselect_81_1 (
    .in_1(in_2[15:8]), .in_2(in_1[15:8]), .sum(carryselect_81_1_sum), .cOut(carryselect_81_1_cout));
  mux2_1 mux2_1_3 (
    .out_4(mux2_1_9_out_4[5]), .in0(carryselect_8_1_sum[5]), .in1(carryselect_81_1_sum[5]),
    .sel(carryselect_8_2_cout));
  mux2_1 mux2_1_4 (
    .out_4(mux2_1_9_out_4[4]), .in0(carryselect_8_1_sum[4]), .in1(carryselect_81_1_sum[4]),
    .sel(carryselect_8_2_cout));
  mux2_1 mux2_1_5 (
    .out_4(mux2_1_9_out_4[3]), .in0(carryselect_8_1_sum[3]), .in1(carryselect_81_1_sum[3]),
    .sel(carryselect_8_2_cout));
  mux2_1 mux2_1_6 (
    .out_4(mux2_1_6_out_4), .in0(carryselect_8_1_cout), .in1(carryselect_81_1_cout),
    .sel(carryselect_8_2_cout));
  CarrySelect_8 carryselect_8_1 (
    .in_1(in_2[15:8]), .in_2(in_1[15:8]), .sum(carryselect_8_1_sum), .cOut(carryselect_8_1_cout));
  mux2_1 mux2_1_7 (
    .out_4(mux2_1_9_out_4[2]), .in0(carryselect_8_1_sum[2]), .in1(carryselect_81_1_sum[2]),
    .sel(carryselect_8_2_cout));
  CarrySelect_8 carryselect_8_2 (.in_1(in_1[7:0]), .in_2(in_2[7:0]), .sum(out_3[7:0]), .cOut(carryselect_8_2_cout));
  assign out_3[15:8] = ~mux2_1_9_out_4;  // NOT_Gate not_1, 8 bits wide
  not not_2 (out_4, mux2_1_6_out_4);
  mux2_1 mux2_1_8 (
    .out_4(mux2_1_9_out_4[1]), .in0(carryselect_8_1_sum[1]), .in1(carryselect_81_1_sum[1]),
    .sel(carryselect_8_2_cout));
  mux2_1 mux2_1_9 (
    .out_4(mux2_1_9_out_4[0]), .in0(carryselect_8_1_sum[0]), .in1(carryselect_81_1_sum[0]),
    .sel(carryselect_8_2_cout));

  // Notes on the sheet:
  //   10.5
  //   12.25
  //   10.5
  //   10.5
  //   10.5
  //   10.5
  //   13
  //   13
  //   Z = max(sel + 1.75, in0 + 1, in1 + 1)
endmodule

module CLA1 (
  input  Cin,
  input  g0,
  input  g1,
  input  g2,
  input  g3,
  input  p0,
  input  p1,
  input  p2,
  input  p3,
  output Cout
);

  wire and_1_out, and_2_out, and_3_out, and_4_out;

  and and_1 (and_1_out, g1, p2, p3);
  and and_2 (and_2_out, g0, p1, p2, p3);
  and and_3 (and_3_out, g2, p3);
  and and_4 (and_4_out, Cin, p0, p1, p2, p3);
  or or_1 (Cout, g3, and_4_out, and_2_out, and_1_out, and_3_out);

  // Notes on the sheet:
  //   48 transistors
endmodule

module CLA2 (
  input  CIn,
  input  G0,
  input  G1,
  input  G2,
  input  G3,
  input  P0,
  input  P1,
  input  P2,
  input  P3,
  output _4_5
);

  wire nand_1_out, nand_2_out, nand_3_out, nand_4_out, nand_5_out, nor_1_out, not_1_out, not_2_out, not_3_out;

  nand nand_1 (nand_1_out, G0, P1, P2, P3);
  nand nand_2 (nand_2_out, G2, P3);
  nand nand_3 (nand_3_out, CIn, P1, P0);
  nand nand_4 (nand_4_out, G1, P2, P3);
  not not_1 (not_1_out, nand_2_out);
  not not_2 (not_2_out, nand_3_out);
  nand nand_5 (nand_5_out, not_2_out, P2, P3);
  not not_3 (not_3_out, nand_4_out);
  nor nor_1 (nor_1_out, G3, not_3_out, not_1_out);
  nand nand_6 (_4_5, nand_5_out, nand_1_out, nor_1_out);

  // Notes on the sheet:
  //   48 transistors
endmodule

module AOI21 (
  input  c,
  input  b,
  input  a,
  output out_4
);

  wire transistor_1_out, transistor_6_out;

  Transistor transistor_1 (.in(1'b1), .out(transistor_1_out), .gate(b));
  Transistor transistor_2 (.in(1'b1), .out(transistor_1_out), .gate(c));
  Transistor transistor_3 (.in(transistor_1_out), .out(out_4), .gate(a));
  Transistor #(.\type ("n")) transistor_4 (.in(transistor_6_out), .out(out_4), .gate(b));
  Transistor #(.\type ("n")) transistor_5 (.in(1'b0), .out(out_4), .gate(a));
  Transistor #(.\type ("n")) transistor_6 (.in(1'b0), .out(transistor_6_out), .gate(c));
endmodule

module CLA3 (
  input  CIn,
  input  G0,
  input  G1,
  input  G2,
  input  G3,
  input  P0,
  input  P1,
  input  P2,
  input  P3,
  output out_10
);

  wire and_1_out, and_2_out, and_3_out, and_4_out, aoi21_1_out_4, or_1_out;

  and and_1 (and_1_out, P2, P3, G1);
  and and_2 (and_2_out, G2, P3);
  and and_3 (and_3_out, P0, P1, P2, P3);
  and and_4 (and_4_out, G0, P1, P2, P3);
  AOI21 aoi21_1 (.out_4(aoi21_1_out_4), .c(CIn), .b(and_3_out), .a(or_1_out));
  or or_1 (or_1_out, and_4_out, and_1_out, and_2_out, G3);
  not not_1 (out_10, aoi21_1_out_4);

  // Notes on the sheet:
  //   50 transistors
endmodule

module Overflow (
  input  A3,
  input  B3,
  input  R3,
  input  OP,
  output out_5
);

  wire multiplexer_1_out, not_1_out, not_2_out, xor_1_out, xor_2_out;

  Multiplexer multiplexer_1 (.in0(B3), .in1(not_1_out), .out(multiplexer_1_out), .sel(OP));
  not not_1 (not_1_out, B3);
  xor xor_1 (xor_1_out, A3, multiplexer_1_out);
  not not_2 (not_2_out, xor_2_out);
  xor xor_2 (xor_2_out, A3, R3);
  nor nor_1 (out_5, xor_1_out, not_2_out);
endmodule

module LALU (
  input  in_1,
  output [15:0] out_2
);

  wire and_1_out, clk, has_op, jmp, jumpn, ld, ldi, mult, mult8_3_1_out_5, multiplexer_1_out, mv, ovfl, r,
       register_2_q, regwe_1_reg0we, regwe_1_reg1we, regwe_1_reg2we, regwe_1_reg3we, st, subtract;
  wire [1:0] Rd, Rs;
  wire [5:0] programcounter_1_pc, targ;
  wire [7:0] ram_1_dout, register_1_q;
  wire [11:0] multiplexer_6_out;
  wire [14:0] addsub16_1_res;
  wire [15:0] dataOut, mult_res, multiplexer_2_out, multiplexer_3_out, multiplexer_4_out, multiplexer_5_out,
       R1, R2, R3, selectD, selectS;

  Multiplexer multiplexer_1 (.in0(jmp), .in1(r), .out(multiplexer_1_out), .sel(jumpn));
  Clock clock_1 (.out(clk));
  programCounter programcounter_1 (
    .clk(clk), .rst(in_1), .jmp(multiplexer_1_out), .targ(targ), .pc(programcounter_1_pc));
  IRDecoder irdecoder_1 (
    .IR(register_1_q), .clk(clk), .rst(in_1), .ld(ld), .ldi(ldi), .sub(subtract), .hasOP(has_op), .mv(mv),
    .st(st), .mult(mult), .jmp(jmp), .jumpn(jumpn), .targ(targ), .RD(Rd), .RS(Rs));
  RAM #(.addrWidth(6), .asyncread("true"), .trigger("falling")) ram_1 (
    .addr(programcounter_1_pc), .we(1'b0), .oe(1'b1), .clk(clk), .dout(ram_1_dout));  // open: din
  srcSel srcsel_1 (.sel(Rd), .reg0(out_2), .reg1(R1), .reg2(R2), .reg3(R3), .regOut(selectD));
  srcSel srcsel_2 (.sel(Rs), .reg0(out_2), .reg1(R1), .reg2(R2), .reg3(R3), .regOut(selectS));
  Register register_1 (.D(ram_1_dout), .en(1'b1), .clk(clk), .Q(register_1_q), .clr(in_1));
  AddSub16 addsub16_1 (.Op(subtract), .A(selectD), .B(selectS), .Res({r, addsub16_1_res}), .overflow(ovfl));
  Multiplexer #(.width(16)) multiplexer_2 (
    .in0({r, addsub16_1_res}), .in1({{14{1'b0}}, Rs}), .out(multiplexer_2_out), .sel(ldi));
  Multiplexer #(.width(16)) multiplexer_3 (.in0(multiplexer_2_out), .in1(dataOut), .out(multiplexer_3_out), .sel(ld));
  Multiplexer #(.width(16)) multiplexer_4 (.in0(multiplexer_3_out), .in1(selectS), .out(multiplexer_4_out), .sel(mv));
  Multiplexer #(.width(16)) multiplexer_5 (
    .in0(multiplexer_4_out), .in1(mult_res), .out(multiplexer_5_out), .sel(mult));
  regWE regwe_1 (
    .Rd(Rd), .regWrite(has_op), .reg0WE(regwe_1_reg0we), .reg1WE(regwe_1_reg1we), .reg2WE(regwe_1_reg2we),
    .reg3WE(regwe_1_reg3we));
  Multiplexer #(.width(12)) multiplexer_6 (
    .in0({12{1'b0}}), .in1({12{1'b1}}), .out(multiplexer_6_out), .sel(mult8_3_1_out_5));
  Mult8_3 mult8_3_1 (
    .in_1(selectD[7:0]), .in_2(selectS[7:0]), .a_neg(selectS[8]), .b_neg(selectD[8]),
    .out_5(mult8_3_1_out_5), .out_6(mult_res));
  and and_1 (and_1_out, has_op, ovfl);
  RAM #(.addrWidth(6), .asyncread("true"), .dataWidth(16), .trigger("falling")) dataMemory (
    .addr({2'b00, selectS[3:0]}), .we(st), .oe(1'b1), .clk(clk), .din(selectD), .dout(dataOut));
  Register #(.width(1)) register_2 (.D(1'b1), .en(and_1_out), .clk(clk), .Q(register_2_q), .clr(in_1));
  Register #(.width(16)) register_3 (.D(multiplexer_5_out), .en(regwe_1_reg0we), .clk(clk), .Q(out_2), .clr(in_1));
  Register #(.width(16)) register_4 (.D(multiplexer_5_out), .en(regwe_1_reg1we), .clk(clk), .Q(R1), .clr(in_1));
  LED led_1 (.in(register_2_q));
  Hex_Digit_Display hex_digit_display_1 (.value(out_2[15:12]));  // open: dp
  Hex_Digit_Display hex_digit_display_2 (.value(out_2[11:8]));  // open: dp
  Hex_Digit_Display hex_digit_display_3 (.value(out_2[7:4]));  // open: dp
  Register #(.width(16)) register_5 (.D(multiplexer_5_out), .en(regwe_1_reg2we), .clk(clk), .Q(R2), .clr(in_1));
  Register #(.width(16)) register_6 (.D(multiplexer_5_out), .en(regwe_1_reg3we), .clk(clk), .Q(R3), .clr(in_1));
  Hex_Digit_Display hex_digit_display_4 (.value(out_2[3:0]));  // open: dp

  // Other names for the same wires on the sheet: R0[15:0] = out_2; rst = in_1
endmodule

module AddSub16 (
  input  Op,
  input  [15:0] A,
  input  [15:0] B,
  output [15:0] Res,
  output overflow
);

  wire not_2_out, xor_1_out, xor_2_out;
  wire [15:0] multiplexer_1_out, not_1_out;

  Multiplexer #(.width(16)) multiplexer_1 (.in0(B), .in1(not_1_out), .out(multiplexer_1_out), .sel(Op));
  assign not_1_out = ~B;  // NOT_Gate not_1, 16 bits wide
  Adder #(.width(16)) adder_1 (.a(A), .b(multiplexer_1_out), .out(Res), .cin(Op));  // open: cout
  xor xor_1 (xor_1_out, A[15], multiplexer_1_out[15]);
  not not_2 (not_2_out, xor_1_out);
  xor xor_2 (xor_2_out, A[15], Res[15]);
  and and_1 (overflow, xor_2_out, not_2_out);
endmodule

module regWE (
  input  [1:0] Rd,
  input  regWrite,
  output reg0WE,
  output reg1WE,
  output reg2WE,
  output reg3WE
);

  wire and_1_out, and_3_out, and_4_out, nor_1_out, not_1_out, not_2_out;

  not not_1 (not_1_out, Rd[1]);
  not not_2 (not_2_out, Rd[0]);
  nor nor_1 (nor_1_out, Rd[1], Rd[0]);
  and and_1 (and_1_out, Rd[0], not_1_out);
  and and_2 (reg1WE, and_1_out, regWrite);
  and and_3 (and_3_out, not_2_out, Rd[1]);
  and and_4 (and_4_out, Rd[0], Rd[1]);
  and and_5 (reg0WE, nor_1_out, regWrite);
  and and_6 (reg2WE, and_3_out, regWrite);
  and and_7 (reg3WE, and_4_out, regWrite);
endmodule

module srcSel (
  input  [1:0] sel,
  input  [15:0] reg0,
  input  [15:0] reg1,
  input  [15:0] reg2,
  input  [15:0] reg3,
  output [15:0] regOut
);

  Multiplexer #(.select(2), .width(16)) multiplexer_1 (
    .in0(reg0), .in1(reg1), .in2(reg2), .in3(reg3), .out(regOut), .sel(sel));
endmodule

module programCounter (
  input  clk,
  input  rst,
  input  jmp,
  input  [5:0] targ,
  output [5:0] pc
);

  wire [5:0] adder_1_out, multiplexer_1_out;

  Adder #(.width(6)) adder_1 (.a(pc), .b(6'b000001), .out(adder_1_out));  // open: cin, cout
  Multiplexer #(.width(6)) multiplexer_1 (.in0(adder_1_out), .in1(targ), .out(multiplexer_1_out), .sel(jmp));
  Register #(.width(6)) register_1 (.D(multiplexer_1_out), .clk(clk), .Q(pc), .clr(rst));  // open: en
endmodule

module IRDecoder (
  input  [7:0] IR,
  input  clk,
  input  rst,
  output ld,
  output ldi,
  output sub,
  output hasOP,
  output mv,
  output st,
  output mult,
  output jmp,
  output jumpn,
  output [5:0] targ,
  output [1:0] RD,
  output [1:0] RS
);

  wire and_1_out, and_2_out, and_3_out, and_4_out, and_5_out, and_6_out, and_8_out, d_ff_3_q, d_ff_8_q,
       nor_1_out, nor_2_out, nor_3_out, not_1_out, not_2_out, not_3_out, not_4_out, not_5_out, not_6_out,
       not_7_out;

  Register #(.width(2)) register_1 (.D(IR[7:6]), .en(1'b1), .clk(clk), .Q(RD), .clr(rst));
  Register #(.width(2)) register_2 (.D(IR[5:4]), .en(1'b1), .clk(clk), .Q(RS), .clr(rst));
  nor nor_1 (nor_1_out, IR[2], IR[3]);
  not not_1 (not_1_out, IR[0]);
  and and_1 (and_1_out, IR[0], IR[1], nor_1_out);
  D_Flip_Flop d_ff_1 (.D(and_1_out), .clk(clk), .Q(sub), .reset(rst));  // open: Qn, preset
  not not_2 (not_2_out, IR[2]);
  and and_2 (and_2_out, IR[2], IR[3], IR[0], IR[1]);
  D_Flip_Flop d_ff_2 (.D(and_3_out), .clk(clk), .Q(ldi), .reset(rst));  // open: Qn, preset
  and and_3 (and_3_out, IR[1], not_1_out, IR[3], IR[2]);
  not not_3 (not_3_out, IR[3]);
  nor nor_2 (nor_2_out, IR[0], IR[1]);
  D_Flip_Flop d_ff_3 (.D(1'b1), .clk(clk), .Q(d_ff_3_q), .reset(rst));  // open: Qn, preset
  D_Flip_Flop d_ff_4 (.D(and_2_out), .clk(clk), .Q(ld), .reset(rst));  // open: Qn, preset
  not not_4 (not_4_out, IR[1]);
  not not_5 (not_5_out, IR[0]);
  not not_6 (not_6_out, IR[3]);
  and and_4 (and_4_out, IR[0], IR[1], not_2_out, IR[3]);
  D_Flip_Flop d_ff_5 (.D(and_5_out), .clk(clk), .Q(mult));  // open: Qn, preset, reset
  and and_5 (and_5_out, not_3_out, IR[2], IR[1], IR[0]);
  nor nor_3 (nor_3_out, IR[3], not_4_out, IR[0], IR[2]);
  D_Flip_Flop d_ff_6 (.D(and_6_out), .clk(clk), .Q(mv), .reset(rst));  // open: Qn, preset
  and and_6 (and_6_out, not_5_out, IR[1], IR[2], not_6_out);
  D_Flip_Flop d_ff_7 (.D(and_4_out), .clk(clk), .Q(st), .reset(rst));  // open: Qn, preset
  and and_7 (jmp, nor_2_out, d_ff_3_q);
  not not_7 (not_7_out, IR[1]);
  and and_8 (and_8_out, IR[0], not_7_out);
  D_Flip_Flop d_ff_8 (.D(nor_3_out), .clk(clk), .Q(d_ff_8_q), .reset(rst));  // open: Qn, preset
  or or_1 (hasOP, d_ff_8_q, sub, mv, ldi, ld, mult);
  and and_9 (jumpn, and_8_out, d_ff_3_q);

  assign targ = IR[7:2];

  // Notes on the sheet:
  //   cOu
endmodule

module PartialProduct (
  input  a8,
  input  a7,
  input  a6,
  input  a5,
  input  a4,
  input  a3,
  input  a2,
  input  a1,
  input  b8,
  input  b7,
  input  b6,
  input  b5,
  input  b4,
  input  b3,
  input  b2,
  input  b1
);

  // AND_Gate and_1 is placed but not wired
  // AND_Gate and_2 is placed but not wired
  // AND_Gate and_3 is placed but not wired
  // AND_Gate and_4 is placed but not wired
  // AND_Gate and_5 is placed but not wired
  // AND_Gate and_6 is placed but not wired
  // AND_Gate and_7 is placed but not wired
  // AND_Gate and_8 is placed but not wired
endmodule

module HardwareMult (
  input  [3:0] in_1,
  input  [3:0] in_2,
  input  b_neg,
  input  a_neg,
  output is_neg,
  output [3:0] out_6,
  output out_7
);

  wire fa40_3_cout;
  wire [0:0] and_16_out, fa40_1_s_2, fa40_2_s_2;
  wire [2:0] and_15_out;
  wire [3:0] and_4_out, and_8_out, and_12_out, fa40_1_s, fa40_2_s, fa40_3_s, multiplexer_1_out,
       multiplexer_2_out, twocomplement_1_out_2, twocomplement_2_out_2, twocomplement_3_out_2;

  Multiplexer #(.width(4)) multiplexer_1 (
    .in0(in_2), .in1(twocomplement_1_out_2), .out(multiplexer_1_out), .sel(b_neg));
  TwoComplement twocomplement_1 (.in_1(in_2), .out_2(twocomplement_1_out_2));  // open: out_3
  and and_1 (and_4_out[3], multiplexer_1_out[3], multiplexer_2_out[3]);
  and and_2 (and_4_out[2], multiplexer_1_out[3], multiplexer_2_out[2]);
  and and_3 (and_4_out[1], multiplexer_1_out[3], multiplexer_2_out[1]);
  and and_4 (and_4_out[0], multiplexer_1_out[3], multiplexer_2_out[0]);
  and and_5 (and_8_out[3], multiplexer_1_out[2], multiplexer_2_out[3]);
  and and_6 (and_8_out[2], multiplexer_1_out[2], multiplexer_2_out[2]);
  and and_7 (and_8_out[1], multiplexer_1_out[2], multiplexer_2_out[1]);
  and and_8 (and_8_out[0], multiplexer_1_out[2], multiplexer_2_out[0]);
  and and_9 (and_12_out[3], multiplexer_1_out[1], multiplexer_2_out[3]);
  xor xor_1 (is_neg, a_neg, b_neg);
  and and_10 (and_12_out[2], multiplexer_1_out[1], multiplexer_2_out[2]);
  and and_11 (and_12_out[1], multiplexer_1_out[1], multiplexer_2_out[1]);
  and and_12 (and_12_out[0], multiplexer_1_out[1], multiplexer_2_out[0]);
  and and_13 (and_15_out[2], multiplexer_1_out[0], multiplexer_2_out[3]);
  and and_14 (and_15_out[1], multiplexer_1_out[0], multiplexer_2_out[2]);
  and and_15 (and_15_out[0], multiplexer_1_out[0], multiplexer_2_out[1]);
  FA40 fa40_1 (.A({1'b0, and_15_out}), .B(and_12_out), .S({fa40_1_s[2:0], fa40_1_s_2[0]}), .COUT(fa40_1_s[3]));
  FA40 fa40_2 (.A(fa40_1_s), .B(and_8_out), .S({fa40_2_s[2:0], fa40_2_s_2[0]}), .COUT(fa40_2_s[3]));
  FA40 fa40_3 (.A(fa40_2_s), .B(and_4_out), .S(fa40_3_s), .COUT(fa40_3_cout));
  or or_1 (out_7, fa40_3_cout, fa40_3_s[3], fa40_3_s[2], fa40_3_s[1]);
  and and_16 (and_16_out[0], multiplexer_2_out[0], multiplexer_1_out[0]);
  TwoComplement twocomplement_2 (.in_1(in_1), .out_2(twocomplement_2_out_2));  // open: out_3
  TwoComplement twocomplement_3 (
    .in_1({fa40_3_s[0], fa40_2_s_2[0], fa40_1_s_2[0], and_16_out[0]}), .out_2(twocomplement_3_out_2));  // open: out_3
  Multiplexer #(.width(4)) multiplexer_2 (
    .in0(in_1), .in1(twocomplement_2_out_2), .out(multiplexer_2_out), .sel(a_neg));
  Multiplexer #(.width(4)) multiplexer_3 (
    .in0({fa40_3_s[0], fa40_2_s_2[0], fa40_1_s_2[0], and_16_out[0]}), .in1(twocomplement_3_out_2),
    .out(out_6), .sel(is_neg));

  // Notes on the sheet:
  //   cOu
endmodule

module TwoComplement (
  input  [3:0] in_1,
  output [3:0] out_2,
  output out_3
);

  wire adder_1_cout, adder_2_cout, adder_3_cout;
  wire [3:0] not_1_out;

  assign not_1_out = ~in_1;  // NOT_Gate not_1, 4 bits wide
  Adder #(.width(1)) adder_1 (.a(not_1_out[0]), .b(1'b1), .out(out_2[0]), .cin(1'b0), .cout(adder_1_cout));
  Adder #(.width(1)) adder_2 (.a(not_1_out[1]), .b(adder_1_cout), .out(out_2[1]), .cout(adder_2_cout));  // open: cin
  Adder #(.width(1)) adder_3 (.a(not_1_out[2]), .b(adder_2_cout), .out(out_2[2]), .cout(adder_3_cout));  // open: cin
  Adder #(.width(1)) adder_4 (.a(not_1_out[3]), .b(adder_3_cout), .out(out_2[3]), .cout(out_3));  // open: cin
endmodule

module HardwareMult2 (
  input  [3:0] in_1,
  input  [3:0] in_2,
  input  b_neg,
  input  a_neg,
  output is_neg,
  output [3:0] out_6,
  output [3:0] out_7
);

  wire [0:0] and_16_out, fa40_1_s_2, fa40_2_s_2, fa40_3_s;
  wire [2:0] and_15_out;
  wire [3:0] and_4_out, and_8_out, and_12_out, fa40_1_s, fa40_2_s, multiplexer_1_out, multiplexer_2_out,
       twocomplement_1_out_2, twocomplement_2_out_2, twocomplement_3_out_2;

  Multiplexer #(.width(4)) multiplexer_1 (
    .in0(in_2), .in1(twocomplement_1_out_2), .out(multiplexer_1_out), .sel(b_neg));
  TwoComplement twocomplement_1 (.in_1(in_2), .out_2(twocomplement_1_out_2));  // open: out_3
  and and_1 (and_4_out[3], multiplexer_1_out[3], multiplexer_2_out[3]);
  and and_2 (and_4_out[2], multiplexer_1_out[3], multiplexer_2_out[2]);
  and and_3 (and_4_out[1], multiplexer_1_out[3], multiplexer_2_out[1]);
  and and_4 (and_4_out[0], multiplexer_1_out[3], multiplexer_2_out[0]);
  and and_5 (and_8_out[3], multiplexer_1_out[2], multiplexer_2_out[3]);
  and and_6 (and_8_out[2], multiplexer_1_out[2], multiplexer_2_out[2]);
  and and_7 (and_8_out[1], multiplexer_1_out[2], multiplexer_2_out[1]);
  and and_8 (and_8_out[0], multiplexer_1_out[2], multiplexer_2_out[0]);
  and and_9 (and_12_out[3], multiplexer_1_out[1], multiplexer_2_out[3]);
  xor xor_1 (is_neg, a_neg, b_neg);
  and and_10 (and_12_out[2], multiplexer_1_out[1], multiplexer_2_out[2]);
  and and_11 (and_12_out[1], multiplexer_1_out[1], multiplexer_2_out[1]);
  and and_12 (and_12_out[0], multiplexer_1_out[1], multiplexer_2_out[0]);
  and and_13 (and_15_out[2], multiplexer_1_out[0], multiplexer_2_out[3]);
  and and_14 (and_15_out[1], multiplexer_1_out[0], multiplexer_2_out[2]);
  and and_15 (and_15_out[0], multiplexer_1_out[0], multiplexer_2_out[1]);
  FA40 fa40_1 (.A({1'b0, and_15_out}), .B(and_12_out), .S({fa40_1_s[2:0], fa40_1_s_2[0]}), .COUT(fa40_1_s[3]));
  FA40 fa40_2 (.A(fa40_1_s), .B(and_8_out), .S({fa40_2_s[2:0], fa40_2_s_2[0]}), .COUT(fa40_2_s[3]));
  FA40 fa40_3 (.A(fa40_2_s), .B(and_4_out), .S({out_7[2:0], fa40_3_s[0]}), .COUT(out_7[3]));
  and and_16 (and_16_out[0], multiplexer_2_out[0], multiplexer_1_out[0]);
  TwoComplement twocomplement_2 (.in_1(in_1), .out_2(twocomplement_2_out_2));  // open: out_3
  TwoComplement twocomplement_3 (
    .in_1({fa40_3_s[0], fa40_2_s_2[0], fa40_1_s_2[0], and_16_out[0]}), .out_2(twocomplement_3_out_2));  // open: out_3
  Multiplexer #(.width(4)) multiplexer_2 (
    .in0(in_1), .in1(twocomplement_2_out_2), .out(multiplexer_2_out), .sel(a_neg));
  Multiplexer #(.width(4)) multiplexer_3 (
    .in0({fa40_3_s[0], fa40_2_s_2[0], fa40_1_s_2[0], and_16_out[0]}), .in1(twocomplement_3_out_2),
    .out(out_6), .sel(is_neg));

  // Notes on the sheet:
  //   cOu
endmodule

module Mult8 (
  input  a_neg,
  input  [7:0] in_2,
  input  [7:0] in_3,
  input  b_neg,
  input  [7:0] in_5,
  output [15:0] out_6
);

  wire xor_1_out;
  wire [3:0] hardwaremult2_2_out_6, hardwaremult2_3_out_6, multiplexer_1_out, multiplexer_1_out_2;
  wire [7:0] twocomplement8_1_out_2;

  HardwareMult2 hardwaremult2_1 (
    .in_1(in_3[7:4]), .in_2(multiplexer_1_out_2), .b_neg(b_neg), .a_neg(a_neg), .out_6(out_6[11:8]));  // open: is_neg, out_7
  TwoComplement8 twocomplement8_1 (.in_1(in_2), .out_2(twocomplement8_1_out_2));  // open: out_3
  HardwareMult2 hardwaremult2_2 (
    .in_1(in_3[3:0]), .in_2(multiplexer_1_out_2), .b_neg(b_neg), .a_neg(a_neg), .out_6(hardwaremult2_2_out_6));  // open: is_neg, out_7
  Multiplexer #(.width(8)) multiplexer_1 (
    .in0(in_2), .in1(twocomplement8_1_out_2), .out({multiplexer_1_out_2, multiplexer_1_out}), .sel(a_neg));
  Adder #(.width(4)) adder_1 (
    .a(hardwaremult2_2_out_6), .b(hardwaremult2_3_out_6), .out(out_6[7:4]));  // open: cin, cout
  HardwareMult2 hardwaremult2_3 (
    .in_1(in_3[7:4]), .in_2(multiplexer_1_out), .b_neg(b_neg), .a_neg(a_neg), .out_6(hardwaremult2_3_out_6));  // open: is_neg, out_7
  Multiplexer #(.width(4)) multiplexer_2 (.in0(4'b0000), .in1(4'b1111), .out(out_6[15:12]), .sel(xor_1_out));
  xor xor_1 (xor_1_out, a_neg, b_neg);
  HardwareMult2 hardwaremult2_4 (
    .in_1(in_3[3:0]), .in_2(multiplexer_1_out), .b_neg(b_neg), .a_neg(a_neg), .out_6(out_6[3:0]));  // open: is_neg, out_7
endmodule

module TwoComplement8 (
  input  [7:0] in_1,
  output [7:0] out_2,
  output out_3
);

  wire adder_1_cout, adder_2_cout, adder_3_cout, adder_4_cout, adder_5_cout, adder_6_cout, adder_7_cout;
  wire [7:0] not_1_out;

  assign not_1_out = ~in_1;  // NOT_Gate not_1, 8 bits wide
  Adder #(.width(1)) adder_1 (.a(not_1_out[0]), .b(1'b1), .out(out_2[0]), .cin(1'b0), .cout(adder_1_cout));
  Adder #(.width(1)) adder_2 (.a(not_1_out[1]), .b(adder_1_cout), .out(out_2[1]), .cout(adder_2_cout));  // open: cin
  Adder #(.width(1)) adder_3 (.a(not_1_out[2]), .b(adder_2_cout), .out(out_2[2]), .cout(adder_3_cout));  // open: cin
  Adder #(.width(1)) adder_4 (.a(not_1_out[3]), .b(adder_3_cout), .out(out_2[3]), .cout(adder_4_cout));  // open: cin
  Adder #(.width(1)) adder_5 (.a(adder_4_cout), .b(not_1_out[4]), .out(out_2[4]), .cout(adder_5_cout));  // open: cin
  Adder #(.width(1)) adder_6 (.a(adder_5_cout), .b(not_1_out[5]), .out(out_2[5]), .cout(adder_6_cout));  // open: cin
  Adder #(.width(1)) adder_7 (.a(adder_6_cout), .b(not_1_out[6]), .out(out_2[6]), .cout(adder_7_cout));  // open: cin
  Adder #(.width(1)) adder_8 (.a(adder_7_cout), .b(not_1_out[7]), .out(out_2[7]), .cout(out_3));  // open: cin
endmodule

module Mult8_2 (
  input  [7:0] in_1,
  input  [7:0] in_2,
  input  b_neg,
  input  a_neg,
  output is_neg,
  output [3:0] out_6,
  output out_7
);

  wire fa40_3_cout;
  wire [0:0] and_16_out, fa40_1_s_2, fa40_2_s_2;
  wire [2:0] and_14_out;
  wire [3:0] and_4_out, and_8_out, and_12_out, fa40_1_s, fa40_2_s, fa40_3_s, twocomplement_1_out_2;
  wire [7:0] multiplexer_1_out, multiplexer_2_out, twocomplement8_1_out_2, twocomplement8_2_out_2;

  TwoComplement8 twocomplement8_1 (.in_1(in_2), .out_2(twocomplement8_1_out_2));  // open: out_3
  and and_1 (and_4_out[3], multiplexer_1_out[3], multiplexer_2_out[3]);
  Multiplexer #(.width(8)) multiplexer_1 (
    .in0(in_2), .in1(twocomplement8_1_out_2), .out(multiplexer_1_out), .sel(b_neg));
  and and_2 (and_4_out[2], multiplexer_1_out[3], multiplexer_2_out[2]);
  and and_3 (and_4_out[1], multiplexer_1_out[3], multiplexer_2_out[1]);
  and and_4 (and_4_out[0], multiplexer_1_out[3], multiplexer_2_out[0]);
  and and_5 (and_8_out[3], multiplexer_1_out[2], multiplexer_2_out[3]);
  and and_6 (and_8_out[2], multiplexer_1_out[2], multiplexer_2_out[2]);
  and and_7 (and_8_out[1], multiplexer_1_out[2], multiplexer_2_out[1]);
  and and_8 (and_8_out[0], multiplexer_1_out[2], multiplexer_2_out[0]);
  xor xor_1 (is_neg, a_neg, b_neg);
  and and_9 (and_12_out[3], multiplexer_1_out[1], multiplexer_2_out[3]);
  and and_10 (and_12_out[2], multiplexer_1_out[1], multiplexer_2_out[2]);
  and and_11 (and_12_out[1], multiplexer_1_out[1], multiplexer_2_out[1]);
  and and_12 (and_12_out[0], multiplexer_1_out[1], multiplexer_2_out[0]);
  and and_13 (and_14_out[1], multiplexer_1_out[0], multiplexer_2_out[2]);
  and and_14 (and_14_out[0], multiplexer_1_out[0], multiplexer_2_out[1]);
  and and_15 (and_14_out[2], multiplexer_1_out[0], multiplexer_2_out[3]);
  FA40 fa40_1 (.A({1'b0, and_14_out}), .B(and_12_out), .S({fa40_1_s[2:0], fa40_1_s_2[0]}), .COUT(fa40_1_s[3]));
  FA40 fa40_2 (.A(fa40_1_s), .B(and_8_out), .S({fa40_2_s[2:0], fa40_2_s_2[0]}), .COUT(fa40_2_s[3]));
  FA40 fa40_3 (.A(fa40_2_s), .B(and_4_out), .S(fa40_3_s), .COUT(fa40_3_cout));
  or or_1 (out_7, fa40_3_cout, fa40_3_s[3], fa40_3_s[2], fa40_3_s[1]);
  and and_16 (and_16_out[0], multiplexer_2_out[0], multiplexer_1_out[0]);
  TwoComplement8 twocomplement8_2 (.in_1(in_1), .out_2(twocomplement8_2_out_2));  // open: out_3
  TwoComplement twocomplement_1 (
    .in_1({fa40_3_s[0], fa40_2_s_2[0], fa40_1_s_2[0], and_16_out[0]}), .out_2(twocomplement_1_out_2));  // open: out_3
  Multiplexer #(.width(8)) multiplexer_2 (
    .in0(in_1), .in1(twocomplement8_2_out_2), .out(multiplexer_2_out), .sel(a_neg));
  Multiplexer #(.width(4)) multiplexer_3 (
    .in0({fa40_3_s[0], fa40_2_s_2[0], fa40_1_s_2[0], and_16_out[0]}), .in1(twocomplement_1_out_2),
    .out(out_6), .sel(is_neg));

  // Notes on the sheet:
  //   cOu
endmodule

module Mult8_3 (
  input  [7:0] in_1,
  input  [7:0] in_2,
  input  a_neg,
  input  b_neg,
  output out_5,
  output [15:0] out_6
);

  wire [3:0] adder_3_out, l_hardwaremult_1_out_6, l_hardwaremult_1_out_7, l_hardwaremult_2_out_6,
       l_hardwaremult_2_out_7, l_hardwaremult_4_out_7, multiplexer_1_out, multiplexer_1_out_2,
       multiplexer_2_out, multiplexer_2_out_2;
  wire [7:0] adder_2_out, l_hardwaremult_3_out_6, twocomplement8_1_out_2, twocomplement8_2_out_2;
  wire [15:0] adder_4_out, l_hardwaremult_4_out_6, not_1_out;

  TwoComplement8 twocomplement8_1 (.in_1(in_2), .out_2(twocomplement8_1_out_2));  // open: out_3
  L_HardwareMult l_hardwaremult_1 (
    .in_1(multiplexer_2_out_2), .in_2(multiplexer_1_out_2), .b_neg(b_neg), .a_neg(a_neg),
    .out_6(l_hardwaremult_1_out_6), .out_7(l_hardwaremult_1_out_7));  // open: is_neg
  Multiplexer #(.width(8)) multiplexer_1 (
    .in0(in_2), .in1(twocomplement8_1_out_2), .out({multiplexer_1_out_2, multiplexer_1_out}), .sel(a_neg));
  Adder adder_1 (
    .a({l_hardwaremult_1_out_7, l_hardwaremult_1_out_6}), .b({4'b0000, adder_3_out}),
    .out(l_hardwaremult_4_out_6[15:8]));  // open: cin, cout
  L_HardwareMult l_hardwaremult_2 (
    .in_1(multiplexer_2_out_2), .in_2(multiplexer_1_out), .b_neg(b_neg), .a_neg(a_neg),
    .out_6(l_hardwaremult_2_out_6), .out_7(l_hardwaremult_2_out_7));  // open: is_neg
  L_HardwareMult l_hardwaremult_3 (
    .in_1(multiplexer_2_out), .in_2(multiplexer_1_out_2), .b_neg(b_neg), .a_neg(a_neg),
    .out_6(l_hardwaremult_3_out_6[3:0]), .out_7(l_hardwaremult_3_out_6[7:4]));  // open: is_neg
  Adder adder_2 (
    .a(l_hardwaremult_3_out_6), .b({l_hardwaremult_2_out_7, l_hardwaremult_2_out_6}), .out(adder_2_out));  // open: cin, cout
  TwoComplement8 twocomplement8_2 (.in_1(in_1), .out_2(twocomplement8_2_out_2));  // open: out_3
  Adder adder_3 (
    .a({4'b0000, l_hardwaremult_4_out_7}), .b(adder_2_out), .out({adder_3_out, l_hardwaremult_4_out_6[7:4]}));  // open: cin, cout
  L_HardwareMult l_hardwaremult_4 (
    .in_1(multiplexer_2_out), .in_2(multiplexer_1_out), .b_neg(b_neg), .a_neg(a_neg),
    .out_6(l_hardwaremult_4_out_6[3:0]), .out_7(l_hardwaremult_4_out_7));  // open: is_neg
  Multiplexer #(.width(8)) multiplexer_2 (
    .in0(in_1), .in1(twocomplement8_2_out_2), .out({multiplexer_2_out_2, multiplexer_2_out}), .sel(b_neg));
  xor xor_1 (out_5, a_neg, b_neg);
  assign not_1_out = ~l_hardwaremult_4_out_6;  // NOT_Gate not_1, 16 bits wide
  Adder #(.width(16)) adder_4 (.a(not_1_out), .b({16{1'b0}}), .out(adder_4_out), .cin(1'b1));  // open: cout
  Multiplexer #(.width(16)) multiplexer_3 (.in0(l_hardwaremult_4_out_6), .in1(adder_4_out), .out(out_6), .sel(out_5));

  // Other names for the same wires on the sheet: is_neg = out_5
endmodule

module L_HardwareMult (
  input  [3:0] in_1,
  input  [3:0] in_2,
  input  b_neg,
  input  a_neg,
  output is_neg,
  output [3:0] out_6,
  output [3:0] out_7
);

  wire [2:0] and_15_out;
  wire [3:0] and_4_out, and_8_out, and_12_out, fa40_1_s, fa40_2_s;

  and and_1 (and_4_out[3], in_2[3], in_1[3]);
  and and_2 (and_4_out[2], in_2[3], in_1[2]);
  and and_3 (and_4_out[1], in_2[3], in_1[1]);
  and and_4 (and_4_out[0], in_2[3], in_1[0]);
  and and_5 (and_8_out[3], in_2[2], in_1[3]);
  and and_6 (and_8_out[2], in_2[2], in_1[2]);
  and and_7 (and_8_out[1], in_2[2], in_1[1]);
  and and_8 (and_8_out[0], in_2[2], in_1[0]);
  and and_9 (and_12_out[3], in_2[1], in_1[3]);
  xor xor_1 (is_neg, a_neg, b_neg);
  and and_10 (and_12_out[2], in_2[1], in_1[2]);
  and and_11 (and_12_out[1], in_2[1], in_1[1]);
  and and_12 (and_12_out[0], in_2[1], in_1[0]);
  and and_13 (and_15_out[2], in_2[0], in_1[3]);
  and and_14 (and_15_out[1], in_2[0], in_1[2]);
  and and_15 (and_15_out[0], in_2[0], in_1[1]);
  FA40 fa40_1 (.A({1'b0, and_15_out}), .B(and_12_out), .S({fa40_1_s[2:0], out_6[1]}), .COUT(fa40_1_s[3]));
  FA40 fa40_2 (.A(fa40_1_s), .B(and_8_out), .S({fa40_2_s[2:0], out_6[2]}), .COUT(fa40_2_s[3]));
  FA40 fa40_3 (.A(fa40_2_s), .B(and_4_out), .S({out_7[2:0], out_6[3]}), .COUT(out_7[3]));
  and and_16 (out_6[0], in_1[0], in_2[0]);

  // Notes on the sheet:
  //   cOu
endmodule
