// Logisim project eight_bit_adder.circ as structural Verilog: 21 circuits, main circuit four_bit_adder_0
module four_bit_adder_0 (
  input  [3:0] a,
  input  [3:0] b,
  output [3:0] Cout,
  output s
);

  wire fa0_1_out2, faopt1_2_cout, faopt2_1_cout;

  faopt1 faopt1_1 (.s(Cout[3]), .cout(s), .b(b[3]), .a(a[3]), .Cin(faopt1_2_cout));
  faopt1 faopt1_2 (.s(Cout[2]), .cout(faopt1_2_cout), .b(b[2]), .a(a[2]), .Cin(faopt2_1_cout));
  faopt2 faopt2_1 (.s(Cout[1]), .Cout(faopt2_1_cout), .Cin(fa0_1_out2), .b(b[1]), .a(a[1]));
  fa0 fa0_1 (.out1(Cout[0]), .out2(fa0_1_out2), .in2(b[0]), .in1(a[0]));

  // Notes on the sheet:
  //   8
  //   9.5
  //   6
  //   6.75
  //   S: 5.5 if Cin < 2.75
  //   Cin + 2.75 if Cin > 2.75
  //   Cout: 2.75 + 2 = 4.75 if Cin < 2.75
  //   Cin + 2 if Cin > 2.75
  //   4
  //   5.5
  //   S: 5.5 if Cin < 2.75
  //   Cin + 2.75 if Cin > 2.75
  //   1.75
  //   2.75
endmodule

module fa0 (
  input  in1,
  input  in2,
  output out1,
  output out2
);

  wire nor_1_out;

  nor nor_1 (nor_1_out, in1, in2);
  and and_1 (out2, in1, in2);
  nor nor_2 (out1, nor_1_out, out2);

  // Notes on the sheet:
  //   14 transistors
  //   FA0
  //   Bhargav Annem
  //   2.75
  //   1.75
endmodule

module faopt2 (
  input  a,
  input  b,
  input  Cin,
  output s,
  output Cout
);

  wire nand_1_out, nand_2_out, nand_3_out, nand_5_out, nor_1_out, nor_2_out, nor_3_out, not_1_out, not_2_out;

  nor nor_1 (nor_1_out, a, b);
  nand nand_1 (nand_1_out, a, b);
  nand nand_2 (nand_2_out, a, Cin);
  nand nand_3 (nand_3_out, Cin, b);
  not not_1 (not_1_out, nand_1_out);
  nor nor_2 (nor_2_out, nor_1_out, not_1_out);
  nand nand_4 (Cout, nand_2_out, nand_3_out, nand_1_out);
  nor nor_3 (nor_3_out, nor_2_out, Cin);
  nand nand_5 (nand_5_out, nor_2_out, Cin);
  not not_2 (not_2_out, nand_5_out);
  nor nor_4 (s, nor_3_out, not_2_out);
endmodule

module faopt1 (
  input  a,
  input  b,
  input  Cin,
  output s,
  output cout
);

  wire nand_1_out, nand_2_out, nor_1_out, nor_2_out, nor_3_out, not_1_out, not_2_out;

  nor nor_1 (nor_1_out, a, b);
  nand nand_1 (nand_1_out, a, b);
  not not_1 (not_1_out, nand_1_out);
  nor nor_2 (nor_2_out, nor_1_out, not_1_out);
  nor nor_3 (nor_3_out, nor_2_out, Cin);
  not not_2 (not_2_out, nand_2_out);
  nand nand_2 (nand_2_out, nor_2_out, Cin);
  nand nand_3 (cout, nand_2_out, nand_1_out);
  nor nor_4 (s, nor_3_out, not_2_out);

  // Notes on the sheet:
  //   0
  //   0
  //   32 Transistors
  //   FAopt1
  //   Bhargav Annem
  //   4.75 if Cin < 2.75
  //   Cin + 2 if Cin >= 2.75
  //   5.5 if Cin < 2.75
  //   Cin + 2.75 if Cin >= 2.75
endmodule

module four_bit_adder_1 (
  input  [3:0] a,
  input  [3:0] b,
  output [3:0] out_3,
  output out_4
);

  wire fa1_1_cout, faopt1_2_cout, faopt2_1_cout;

  faopt1 faopt1_1 (.s(out_3[3]), .cout(out_4), .b(b[3]), .a(a[3]), .Cin(faopt1_2_cout));
  faopt1 faopt1_2 (.s(out_3[2]), .cout(faopt1_2_cout), .b(b[2]), .a(a[2]), .Cin(faopt2_1_cout));
  faopt2 faopt2_1 (.s(out_3[1]), .Cout(faopt2_1_cout), .Cin(fa1_1_cout), .b(b[1]), .a(a[1]));
  fa1 fa1_1 (.s(out_3[0]), .Cout(fa1_1_cout), .a(a[0]), .b(b[0]));

  // Notes on the sheet:
  //   8
  //   9.5
  //   6
  //   6.75
  //   S: 5.5 if Cin < 2.75
  //   Cin + 2.75 if Cin > 2.75
  //   Cout: 2.75 + 2 = 4.75 if Cin < 2.75
  //   Cin + 2 if Cin > 2.75
  //   4
  //   5.5
  //   S: 5.5 if Cin < 2.75
  //   Cin + 2.75 if Cin > 2.75
  //   1.75
  //   2.75
endmodule

module fa1 (
  input  a,
  input  b,
  output s,
  output Cout
);

  wire nand_1_out;

  nand nand_1 (nand_1_out, a, b);
  or or_1 (Cout, a, b);
  nand nand_2 (s, nand_1_out, Cout);
endmodule

module eight_but_carry_0 (
  input  [7:0] a,
  input  [7:0] b,
  output [7:0] Cout,
  output s
);

  wire four_bit_adder_0_1_s, four_bit_adder_0_2_s, four_bit_adder_1_1_out_4, mux2i_1_z, mux2i_2_z, mux2i_3_z,
       mux2i_4_z, mux2i_5_z;
  wire [3:0] four_bit_adder_0_1_cout, four_bit_adder_1_1_out_3;

  four_bit_adder_1 four_bit_adder_1_1 (
    .out_3(four_bit_adder_1_1_out_3), .out_4(four_bit_adder_1_1_out_4), .b(b[7:4]), .a(a[7:4]));
  four_bit_adder_0 four_bit_adder_0_1 (
    .Cout(four_bit_adder_0_1_cout), .s(four_bit_adder_0_1_s), .b(b[7:4]), .a(a[7:4]));
  not not_1 (s, mux2i_1_z);
  mux2i mux2i_1 (.z(mux2i_1_z), .in0(four_bit_adder_0_1_s), .in1(four_bit_adder_1_1_out_4), .sel(four_bit_adder_0_2_s));
  not not_2 (Cout[4], mux2i_2_z);
  mux2i mux2i_2 (
    .z(mux2i_2_z), .in0(four_bit_adder_0_1_cout[0]), .in1(four_bit_adder_1_1_out_3[0]),
    .sel(four_bit_adder_0_2_s));
  mux2i mux2i_3 (
    .z(mux2i_3_z), .in0(four_bit_adder_0_1_cout[1]), .in1(four_bit_adder_1_1_out_3[1]),
    .sel(four_bit_adder_0_2_s));
  mux2i mux2i_4 (
    .z(mux2i_4_z), .in0(four_bit_adder_0_1_cout[2]), .in1(four_bit_adder_1_1_out_3[2]),
    .sel(four_bit_adder_0_2_s));
  not not_3 (Cout[5], mux2i_3_z);
  not not_4 (Cout[6], mux2i_4_z);
  mux2i mux2i_5 (
    .z(mux2i_5_z), .in0(four_bit_adder_0_1_cout[3]), .in1(four_bit_adder_1_1_out_3[3]),
    .sel(four_bit_adder_0_2_s));
  not not_5 (Cout[7], mux2i_5_z);
  four_bit_adder_0 four_bit_adder_0_2 (.Cout(Cout[3:0]), .s(four_bit_adder_0_2_s), .b(b[3:0]), .a(a[3:0]));

  // Notes on the sheet:
  //   8
  //   8
  //   8
  //   10.5
  //   8
  //   9.75
  //   9.75
  //   9.75
  //   9.75
  //   10.5
  //   8
  //   8-bit carry Select
  //   Bhargav Annem
  //   10.5
endmodule

module mux2 (
  input  a,
  input  b,
  input  s,
  output z
);

  wire nand_1_out, nand_2_out, not_1_out;

  not not_1 (not_1_out, s);
  nand nand_1 (nand_1_out, a, not_1_out);
  nand nand_2 (nand_2_out, b, s);
  nand nand_3 (z, nand_1_out, nand_2_out);
endmodule

module mux4 (
  input  in0,
  input  in1,
  input  in2,
  input  in3,
  input  s0,
  input  s1,
  output z
);

  wire mux2_1_z, mux2_2_z;

  mux2 mux2_1 (.z(mux2_1_z), .a(in0), .b(in1), .s(s0));
  mux2 mux2_2 (.z(mux2_2_z), .a(in2), .b(in3), .s(s0));
  mux2 mux2_3 (.z(z), .a(mux2_1_z), .b(mux2_2_z), .s(s1));
endmodule

module mux2i (
  input  in0,
  input  in1,
  input  sel,
  output z
);

  wire transmission_1_p3, transmission_1_p4;

  // Transmission_Gate transmission_1: pin names not known; wires that end beside it: in0, sel, transmission_1_p3, transmission_1_p4
  not not_1 (transmission_1_p3, sel);
  // Transmission_Gate transmission_2: pin names not known; wires that end beside it: in1, transmission_1_p3, sel, transmission_1_p4
  not not_2 (z, transmission_1_p4);
endmodule

module mux4i (
  input  in_1,
  input  in_2,
  input  in_3,
  input  in_4,
  input  in_5,
  input  in_6,
  output out_7
);

  wire mux2i_1_z, mux2i_3_z;

  mux2i mux2i_1 (.z(mux2i_1_z), .in0(in_1), .in1(in_2), .sel(in_5));
  mux2i mux2i_2 (.z(out_7), .in0(mux2i_1_z), .in1(mux2i_3_z), .sel(in_6));
  mux2i mux2i_3 (.z(mux2i_3_z), .in0(in_3), .in1(in_4), .sel(in_5));
endmodule

module eight_bit_carry_1 (
  input  [7:0] a,
  input  [7:0] b,
  output [7:0] Cout,
  output s
);

  wire four_bit_adder_0_1_s, four_bit_adder_1_1_out_4, four_bit_adder_1_2_out_4, mux2i_1_z, mux2i_2_z,
       mux2i_3_z, mux2i_4_z, mux2i_5_z;
  wire [3:0] four_bit_adder_0_1_cout, four_bit_adder_1_1_out_3;

  four_bit_adder_1 four_bit_adder_1_1 (
    .out_3(four_bit_adder_1_1_out_3), .out_4(four_bit_adder_1_1_out_4), .b(b[7:4]), .a(a[7:4]));
  four_bit_adder_0 four_bit_adder_0_1 (
    .Cout(four_bit_adder_0_1_cout), .s(four_bit_adder_0_1_s), .b(b[7:4]), .a(a[7:4]));
  not not_1 (s, mux2i_1_z);
  mux2i mux2i_1 (
    .z(mux2i_1_z), .in0(four_bit_adder_0_1_s), .in1(four_bit_adder_1_1_out_4), .sel(four_bit_adder_1_2_out_4));
  not not_2 (Cout[4], mux2i_2_z);
  mux2i mux2i_2 (
    .z(mux2i_2_z), .in0(four_bit_adder_0_1_cout[0]), .in1(four_bit_adder_1_1_out_3[0]),
    .sel(four_bit_adder_1_2_out_4));
  mux2i mux2i_3 (
    .z(mux2i_3_z), .in0(four_bit_adder_0_1_cout[1]), .in1(four_bit_adder_1_1_out_3[1]),
    .sel(four_bit_adder_1_2_out_4));
  mux2i mux2i_4 (
    .z(mux2i_4_z), .in0(four_bit_adder_0_1_cout[2]), .in1(four_bit_adder_1_1_out_3[2]),
    .sel(four_bit_adder_1_2_out_4));
  not not_3 (Cout[5], mux2i_3_z);
  not not_4 (Cout[6], mux2i_4_z);
  mux2i mux2i_5 (
    .z(mux2i_5_z), .in0(four_bit_adder_0_1_cout[3]), .in1(four_bit_adder_1_1_out_3[3]),
    .sel(four_bit_adder_1_2_out_4));
  not not_5 (Cout[7], mux2i_5_z);
  four_bit_adder_1 four_bit_adder_1_2 (.out_3(Cout[3:0]), .out_4(four_bit_adder_1_2_out_4), .b(b[3:0]), .a(a[3:0]));

  // Notes on the sheet:
  //   8
  //   8
  //   8
  //   10.5
  //   8
  //   9.75
  //   9.75
  //   9.75
  //   9.75
  //   10.5
  //   8
  //   8-bit carry Select
  //   Bhargav Annem
  //   8
  //   10.5
endmodule

module sixteen_bit_carry_0 (
  input  Cin,
  input  [15:0] a,
  input  [15:0] b,
  output [15:0] Cout,
  output s
);

  wire _13_z, eight_bit_carry_1_1_s, eight_bit_carry_1_2_s, eight_but_carry_0_1_s, eight_but_carry_0_2_s,
       multiplexer_2_out, mux2i_1_z, mux2i_2_z, mux2i_3_z, mux2i_4_z, mux2i_5_z, mux2i_6_z, mux2i_7_z,
       mux2i_8_z, not_1_out;
  wire [7:0] eight_bit_carry_1_1_cout, eight_bit_carry_1_2_cout, eight_but_carry_0_1_cout,
       eight_but_carry_0_2_cout;

  eight_bit_carry_1 eight_bit_carry_1_1 (
    .s(eight_bit_carry_1_1_s), .Cout(eight_bit_carry_1_1_cout), .b(b[15:8]), .a(a[15:8]));
  not not_1 (not_1_out, Cin);
  eight_but_carry_0 eight_but_carry_0_1 (
    .s(eight_but_carry_0_1_s), .Cout(eight_but_carry_0_1_cout), .b(b[15:8]), .a(a[15:8]));
  mux2i mux2i_1 (
    .z(mux2i_1_z), .in0(eight_but_carry_0_1_cout[0]), .in1(eight_bit_carry_1_1_cout[0]),
    .sel(multiplexer_2_out));
  mux2i mux2i_2 (
    .z(mux2i_2_z), .in0(eight_but_carry_0_1_cout[1]), .in1(eight_bit_carry_1_1_cout[1]),
    .sel(multiplexer_2_out));
  mux2i mux2i_3 (
    .z(mux2i_3_z), .in0(eight_but_carry_0_1_cout[2]), .in1(eight_bit_carry_1_1_cout[2]),
    .sel(multiplexer_2_out));
  mux2i mux2i_4 (
    .z(mux2i_4_z), .in0(eight_but_carry_0_1_cout[3]), .in1(eight_bit_carry_1_1_cout[3]),
    .sel(multiplexer_2_out));
  mux2i mux2i_5 (
    .z(mux2i_5_z), .in0(eight_but_carry_0_1_cout[4]), .in1(eight_bit_carry_1_1_cout[4]),
    .sel(multiplexer_2_out));
  mux2i _13 (.z(_13_z), .in0(eight_but_carry_0_1_cout[5]), .in1(eight_bit_carry_1_1_cout[5]), .sel(multiplexer_2_out));
  mux2i mux2i_6 (
    .z(mux2i_6_z), .in0(eight_but_carry_0_1_cout[6]), .in1(eight_bit_carry_1_1_cout[6]),
    .sel(multiplexer_2_out));
  not not_2 (Cout[8], mux2i_1_z);
  not not_3 (Cout[9], mux2i_2_z);
  not not_4 (Cout[10], mux2i_3_z);
  not not_5 (Cout[11], mux2i_4_z);
  not not_6 (Cout[12], mux2i_5_z);
  not not_7 (Cout[13], _13_z);
  not not_8 (Cout[14], mux2i_6_z);
  not not_9 (Cout[15], mux2i_7_z);
  mux2i mux2i_7 (
    .z(mux2i_7_z), .in0(eight_but_carry_0_1_cout[7]), .in1(eight_bit_carry_1_1_cout[7]),
    .sel(multiplexer_2_out));
  eight_but_carry_0 eight_but_carry_0_2 (
    .s(eight_but_carry_0_2_s), .Cout(eight_but_carry_0_2_cout), .b(b[7:0]), .a(a[7:0]));
  mux2i mux2i_8 (.z(mux2i_8_z), .in0(eight_but_carry_0_1_s), .in1(eight_bit_carry_1_1_s), .sel(multiplexer_2_out));
  not not_10 (s, mux2i_8_z);
  eight_bit_carry_1 eight_bit_carry_1_2 (
    .s(eight_bit_carry_1_2_s), .Cout(eight_bit_carry_1_2_cout), .b(b[7:0]), .a(a[7:0]));
  Multiplexer #(.width(8)) multiplexer_1 (
    .in0(eight_bit_carry_1_2_cout), .in1(eight_but_carry_0_2_cout), .out(Cout[7:0]), .sel(not_1_out));
  Multiplexer multiplexer_2 (
    .in0(eight_bit_carry_1_2_s), .in1(eight_but_carry_0_2_s), .out(multiplexer_2_out), .sel(not_1_out));

  // Notes on the sheet:
  //   10.5
  //   10.5
  //   10.5
  //   12.25
  //   10.5
  //   After all of the mex's, the time is 12.25
  //   10.5
  //   13
  //   13
  //   1
  //   16-bit carry Select
  //   Bhargav Annem
endmodule

module cla (
  input  G3,
  input  G2,
  input  G1,
  input  G0,
  input  Cin,
  input  P3,
  input  P2,
  input  P1,
  input  P0,
  output Cout
);
endmodule

module cla_unopt (
  input  G0,
  input  G1,
  input  G2,
  input  G3,
  input  Cin,
  input  P0,
  input  P1,
  input  P2,
  input  P3,
  output Cout
);

  wire and_1_out, and_2_out, and_3_out, and_4_out;

  and and_1 (and_1_out, P3, G2);
  and and_2 (and_2_out, G1, P2, P3);
  and and_3 (and_3_out, G0, P1, P2, P3);
  and and_4 (and_4_out, Cin, P0, P1, P2, P3);
  or or_1 (Cout, G3, and_1_out, and_2_out, and_3_out, and_4_out);
endmodule

module adder_16 (
  input  subtr,
  input  [15:0] Rd,
  input  [15:0] Ra,
  output [15:0] sum,
  output ovr
);

  wire xnor_1_out, xor_1_out;
  wire [15:0] multiplexer_1_out, not_1_out;

  Multiplexer #(.width(16)) multiplexer_1 (.in0(Ra), .in1(not_1_out), .out(multiplexer_1_out), .sel(subtr));
  assign not_1_out = ~Ra;  // NOT_Gate not_1, 16 bits wide
  sixteen_bit_carry_0 sixteen_bit_carry_0_1 (.Cin(subtr), .a(Rd), .b(multiplexer_1_out), .Cout(sum));  // open: s
  xnor xnor_1 (xnor_1_out, Rd[15], multiplexer_1_out[15]);
  xor xor_1 (xor_1_out, sum[15], Rd[15]);
  and and_1 (ovr, xor_1_out, xnor_1_out);
endmodule

module alu (
  input  rst,
  input  [13:0] in_2
);

  wire add_or_sub, and_1_out, clk, ld, ldi, or_1_out, ovrfl, pow, R0_sel, R1_sel, R2_sel, R3_sel,
       register_2_q, subtr;
  wire [1:0] Rd, Rs;
  wire [7:0] counter, ram_1_dout, register_1_q;
  wire [15:0] add_sub, load_data, multiplexer_1_out, R0_out, R1_out, R2_out, R3_out, ram_2_dout, Rd_in, res,
       Rs_in;

  Clock u_clk (.out(clk));
  programCounter programcounter_1 (.clk(clk), .rst(rst), .out_3(counter));
  RAM #(.trigger("falling")) ram_1 (.addr(counter), .we(1'b0), .oe(1'b1), .clk(clk), .dout(ram_1_dout));  // open: din
  or or_1 (or_1_out, ldi, ld);
  Register register_1 (.D(ram_1_dout), .en(1'b1), .clk(clk), .Q(register_1_q), .clr(rst));
  RAM #(.addrWidth(4), .dataWidth(16), .trigger("falling")) ram_2 (
    .addr(Rs_in[3:0]), .we(1'b0), .oe(1'b1), .clk(clk), .dout(ram_2_dout));  // open: din
  regWE regwe_1 (.regWrite(pow), .Rd(Rd), .reg0WE(R0_sel), .reg1WE(R1_sel), .reg2WE(R2_sel), .reg3WE(R3_sel));
  adder_16 adder_16_1 (.subtr(add_or_sub), .Rd(Rs_in), .Ra(Rd_in), .sum(add_sub), .ovr(ovrfl));
  srcSelect srcselect_1 (.reg0(R0_out), .reg1(R1_out), .reg2(R2_out), .reg3(R3_out), .sel(Rd), .regOut(Rs_in));
  srcSelect srcselect_2 (.reg0(R0_out), .reg1(R1_out), .reg2(R2_out), .reg3(R3_out), .sel(Rs), .regOut(Rd_in));
  and and_1 (and_1_out, ovrfl, pow);
  IRDecoder irdecoder_1 (
    .IR(register_1_q), .clk(clk), .rst(rst), .add_or_sub(add_or_sub), .Rs(Rs), .sub(subtr), .Rd(Rd),
    .pow(pow), .ldi(ldi), .ld(ld));
  Multiplexer #(.width(16)) multiplexer_1 (.in0(add_sub), .in1(ram_2_dout), .out(multiplexer_1_out), .sel(ld));
  Register #(.width(16)) R0 (.D(res), .en(R0_sel), .clk(clk), .Q(R0_out), .clr(rst));
  Register #(.width(16)) R2 (.D(res), .en(R2_sel), .clk(clk), .Q(R2_out), .clr(rst));
  Register #(.width(1)) register_2 (.D(1'b1), .en(and_1_out), .clk(clk), .Q(register_2_q), .clr(rst));
  LED led_1 (.in(register_2_q));
  Multiplexer #(.width(16)) multiplexer_2 (.in0(multiplexer_1_out), .in1({in_2, Rs}), .out(load_data), .sel(ldi));
  Multiplexer #(.width(16)) multiplexer_3 (.in0(add_sub), .in1(load_data), .out(res), .sel(add_or_sub));
  Register #(.width(16)) R1 (.D(res), .en(R1_sel), .clk(clk), .Q(R1_out), .clr(rst));
  Register #(.width(16)) R3 (.D(res), .en(R3_sel), .clk(clk), .Q(R3_out), .clr(rst));

  // Notes on the sheet:
  //   b3 43 e2 32 82
  //   4C 41 53 41 7B 43 53 7D
endmodule

module regWE (
  input  regWrite,
  input  [1:0] Rd,
  output reg0WE,
  output reg1WE,
  output reg2WE,
  output reg3WE
);

  wire reg0WE_t, reg1WE_t, reg2WE_t, reg3WE_t, xor_1_out;

  xor xor_1 (xor_1_out, Rd[0], Rd[1]);
  and and_1 (reg3WE_t, Rd[0], Rd[1]);
  nor nor_1 (reg0WE_t, Rd[0], Rd[1]);
  and and_2 (reg1WE_t, xor_1_out, Rd[0]);
  and and_3 (reg2WE_t, xor_1_out, Rd[1]);
  and and_4 (reg0WE, regWrite, reg0WE_t);
  and and_5 (reg1WE, regWrite, reg1WE_t);
  and and_6 (reg2WE, regWrite, reg2WE_t);
  and and_7 (reg3WE, regWrite, reg3WE_t);
endmodule

module srcSelect (
  input  [15:0] reg0,
  input  [15:0] reg1,
  input  [15:0] reg2,
  input  [15:0] reg3,
  input  [1:0] sel,
  output [15:0] regOut
);

  Multiplexer #(.select(2), .width(16)) multiplexer_1 (
    .in0(reg0), .in1(reg1), .in2(reg2), .in3(reg3), .out(regOut), .sel(sel));
endmodule

module programCounter (
  input  clk,
  input  rst,
  output [7:0] out_3
);

  wire [7:0] adder_1_out;

  Adder adder_1 (.a(out_3), .b(8'h1), .out(adder_1_out));  // open: cin, cout
  Register register_1 (.D(adder_1_out), .en(1'b1), .clk(clk), .Q(out_3), .clr(rst));
endmodule

module IRDecoder (
  input  [7:0] IR,
  input  clk,
  input  rst,
  output add_or_sub,
  output [1:0] Rs,
  output sub,
  output [1:0] Rd,
  output pow,
  output ldi,
  output ld
);

  wire and_1_out, and_2_out, and_3_out, and_4_out, and_5_out, and_6_out, nor_1_out, not_1_out, not_2_out,
       not_3_out, not_4_out, not_5_out, not_6_out, or_1_out, xor_1_out;

  D_Flip_Flop d_ff_1 (.D(IR[4]), .clk(clk), .Q(Rs[0]), .reset(rst));  // open: Qn, preset
  D_Flip_Flop d_ff_2 (.D(IR[5]), .clk(clk), .Q(Rs[1]), .reset(rst));  // open: Qn, preset
  D_Flip_Flop d_ff_3 (.D(IR[6]), .clk(clk), .Q(Rd[0]), .reset(rst));  // open: Qn, preset
  D_Flip_Flop d_ff_4 (.D(IR[7]), .clk(clk), .Q(Rd[1]), .reset(rst));  // open: Qn, preset
  not not_1 (not_1_out, IR[3]);
  not not_2 (not_2_out, IR[2]);
  not not_3 (not_3_out, IR[0]);
  nor nor_1 (nor_1_out, IR[3], IR[2]);
  and and_1 (and_1_out, IR[1], IR[0]);
  not not_4 (not_4_out, IR[0]);
  and and_2 (and_2_out, not_4_out, IR[1], not_5_out, not_6_out);
  not not_5 (not_5_out, IR[2]);
  not not_6 (not_6_out, IR[3]);
  and and_3 (and_3_out, nor_1_out, and_1_out);
  and and_4 (and_4_out, not_1_out, not_2_out, IR[1], not_3_out);
  and and_5 (and_5_out, IR[3], IR[2], IR[2], not_3_out);
  and and_6 (and_6_out, IR[3], IR[2], IR[2], IR[0]);
  D_Flip_Flop d_ff_5 (.D(or_1_out), .clk(clk), .Q(add_or_sub), .reset(rst));  // open: Qn, preset
  or or_1 (or_1_out, and_2_out, and_3_out);
  D_Flip_Flop d_ff_6 (.D(and_3_out), .clk(clk), .Q(sub), .reset(rst));  // open: Qn, preset
  D_Flip_Flop d_ff_7 (.D(xor_1_out), .clk(clk), .Q(pow), .reset(rst));  // open: Qn, preset
  ExactlyOne xor_1 (.out(xor_1_out), .in0(and_3_out), .in1(and_5_out), .in2(and_6_out), .in3(and_4_out));
  D_Flip_Flop d_ff_8 (.D(and_5_out), .clk(clk), .Q(ldi), .reset(rst));  // open: Qn, preset
  D_Flip_Flop d_ff_9 (.D(and_6_out), .clk(clk), .Q(ld), .reset(rst));  // open: Qn, preset

  // Notes on the sheet:
  //   r
endmodule
